# Fritzing sketch gauges_sensor_shield (saved by Fritzing 0.8.5b)

parts:
  Part1 = Arduino ProtoShield
  J1 = female pin header, 6 pins [form="♀ (female)"]
  R1 = Resistor [tolerance=±5% resistance=100k package=THT]
  R2 = Resistor [tolerance=±5% resistance=10k package=THT]
  R3 = Resistor [tolerance=±5% resistance=10k package=THT]

nets (from the schematic view):
  N1: Part1.A0, Part1.N$54, R3.Pin_1
  N2: Part1.N$51, R1.Pin_1
  N3: Part1.N$52, Part1.N$58, R2.Pin_1, R3.Pin_0
  N4: Part1.N$95, Part1.N$181, J1.pin6, R1.Pin_0
  N5: Part1.N$96, R2.Pin_0
  N6: Part1.N$176, J1.pin1
  N7: Part1.N$177, J1.pin2
  N8: Part1.N$178, J1.pin3
  N9: Part1.N$179, J1.pin4
  N10: Part1.N$180, J1.pin5
