# Fritzing sketch gauges_arduino_nano_input_shield (saved by Fritzing 0.8.5b)
circuit board: 10cm x 7.5cm
breadboards: 1

parts:
  J5 = male pin header, 2 pins [form="♂ (male)"]
  C1 = Electrolytic Capacitor [capacitance=10µF voltage=50V package="100 mil [THT, electrolytic]"]
  C2 = Ceramic Capacitor [capacitance=100nF package="100 mil [THT, multilayer]"]
  J9 = male pin header, 4 pins [form="♂ (male)"]
  Part1 = Arduino Nano (Rev3.0)
  U3 = Optocoupler [package=THT]
  R2 = Resistor [tolerance=±5% resistance=330 package=THT]
  D14 = Rectifier Diode [part_number=1N4001 package="300 mil [THT]"]
  U4 = Optocoupler [package=THT]
  R3 = Resistor [tolerance=±5% resistance=330 package=THT]
  D15 = Rectifier Diode [part_number=1N4001 package="300 mil [THT]"]
  U5 = Optocoupler [package=THT]
  R4 = Resistor [tolerance=±5% resistance=330 package=THT]
  D16 = Rectifier Diode [part_number=1N4001 package="300 mil [THT]"]
  U6 = Voltage Regulator - 9V [package="TO220 [THT]"]
  J10 = female pin header, 4 pins [form="♀ (female)"]
  R10 = Resistor [tolerance=±5% resistance=10k package=THT]
  R11 = Resistor [tolerance=±5% resistance=15k package=THT]
  J11 = female pin header, 2 pins [form="♀ (female)"]
  D17 = Schottky Diode [part_number=1N5817 package="300 mil [THT]"]
  D18 = Schottky Diode [part_number=1N5817 package="300 mil [THT]"]
  R12 = Resistor [tolerance=±5% resistance=10k package=THT]
  C5 = Ceramic Capacitor [capacitance=0.1µF voltage=20V package="100 mil [THT, multilayer]"]
  R13 = Resistor [tolerance=±5% resistance=2.2k package=THT]
  J12 = female pin header, 2 pins [form="♀ (female)"]
  D19 = Schottky Diode [part_number=1N5817 package="300 mil [THT]"]
  D20 = Schottky Diode [part_number=1N5817 package="300 mil [THT]"]
  R14 = Resistor [tolerance=±5% resistance=10k package=THT]
  C6 = Ceramic Capacitor [capacitance=0.1µF voltage=20V package="100 mil [THT, multilayer]"]
  R15 = Resistor [tolerance=±5% resistance=2.2k package=THT]
  J13 = female pin header, 2 pins [form="♀ (female)"]
  D21 = Schottky Diode [part_number=1N5817 package="300 mil [THT]"]
  D22 = Schottky Diode [part_number=1N5817 package="300 mil [THT]"]
  R16 = Resistor [tolerance=±5% resistance=10k package=THT]
  C7 = Ceramic Capacitor [capacitance=0.1µF voltage=20V package="100 mil [THT, multilayer]"]
  R17 = Resistor [tolerance=±5% resistance=100 package=THT]
  J14 = female pin header, 2 pins [form="♀ (female)"]
  D23 = Schottky Diode [part_number=1N5817 package="300 mil [THT]"]
  D24 = Schottky Diode [part_number=1N5817 package="300 mil [THT]"]
  R18 = Resistor [tolerance=±5% resistance=10k package=THT]
  C8 = Ceramic Capacitor [capacitance=0.1µF voltage=20V package="100 mil [THT, multilayer]"]

nets (from the schematic view):
  GND: J5.pin1, C1.-, C2.0, J9.pin1, Part1.GND, U3.Pin_2, U3.Pin_4, D14.anode, U4.Pin_2, U4.Pin_4, D15.anode, U5.Pin_2, U5.Pin_4, D16.anode, U6.GND, R10.Pin_1, D17.anode, C5.0, D20.anode, C6.0, D22.anode, C7.0, D23.anode, C8.0
  N1: J5.pin2, U6.input_voltage
  N2: C1.+, C2.1, Part1.VIN, U6.output_voltage, R11.Pin_0, D18.cathode, R13.Pin_0, D19.cathode, R15.Pin_0, D21.cathode, R17.Pin_0, D24.cathode
  N3: J9.pin2, R3.Pin_0
  N4: J9.pin3, R4.Pin_0
  N5: J9.pin4, R2.Pin_0
  N6: Part1.D3, U4.Pin_5
  N7: Part1.D6, J10.pin1
  N8: Part1.D7, J10.pin2
  N9: Part1.D8, J10.pin3
  N10: Part1.D9, J10.pin4
  N11: Part1.D10, U5.Pin_5
  N12: Part1.D11/MOSI, U3.Pin_5
  N13: Part1.A3, D23.cathode, D24.anode, R18.Pin_1, C8.1
  N14: Part1.A2, D21.anode, D22.cathode, R16.Pin_1, C7.1
  N15: Part1.A1, D19.anode, D20.cathode, R14.Pin_1, C6.1
  N16: Part1.A0, D17.cathode, D18.anode, R12.Pin_1, C5.1
  N17: U3.Pin_1, R2.Pin_1, D14.cathode
  N18: U4.Pin_1, R3.Pin_1, D15.cathode
  N19: U5.Pin_1, R4.Pin_1, D16.cathode
  N20: R10.Pin_0, R11.Pin_1, J11.pin2, R12.Pin_0
  N21: R13.Pin_1, J12.pin2, R14.Pin_0
  N22: R15.Pin_1, J13.pin2, R16.Pin_0
  N23: R17.Pin_1, J14.pin2, R18.Pin_0

custom parts:
  Voltage Regulator - 9V: 9V DC Voltage Regulator
