# Fritzing sketch speedo_arduino_uno_shield (saved by Fritzing 0.8.5b)
circuit board: 6.9215cm x 5.33756cm
breadboards: 1

parts:
  J5 = male pin header, 2 pins [form="♂ (male)"]
  J6 = male pin header, 3 pins [form="♂ (male)"]
  C1 = Electrolytic Capacitor [capacitance=10µF voltage=50V package="100 mil [THT, electrolytic]"]
  C2 = Ceramic Capacitor [capacitance=100nF package="100 mil [THT, multilayer]"]
  U2 = Optocoupler [package=THT]
  R1 = Resistor [tolerance=±5% resistance=330 package=THT]
  D13 = Rectifier Diode [part_number=1N4001 package="300 mil [THT]"]
  R2 = Resistor [tolerance=±5% resistance=100k package=THT]
  J7 = male pin header, 2 pins [form="♂ (male)"]
  J8 = male pin header, 2 pins [form="♂ (male)"]
  Part1 = Arduino Uno (Rev3)
  J9 = male pin header, 4 pins [form="♂ (male)"]
  J10 = female pin header, 3 pins [form="♀ (female)"]

nets:
  GND: J5.pin1, J6.pin1, C1.-, C2.0, U2.Pin_2, U2.Pin_4, D13.anode, J7.pin1, J8.pin1, Part1.GND, J9.pin4
  N1: J5.pin2, J6.pin3, C1.+, C2.1, Part1.VIN
  N2: J6.pin2, R1.Pin_0
  N3: U2.Pin_1, R1.Pin_1, D13.cathode
  N4: U2.Pin_5, R2.Pin_0, Part1.D2
  N5: R2.Pin_1, Part1.5V
  N6: J7.pin2, Part1.D4
  N7: J8.pin2, Part1.D5_PWM
  N8: Part1.D8, J10.pin2
  N9: Part1.D9_PWM, J10.pin3
  N10: Part1.D11_PWM/MOSI, J9.pin2
  N11: Part1.D12/MISO, J9.pin3
  N12: Part1.D3_PWM, J9.pin1
  N13: Part1.D7, J10.pin1
